# Fritzing sketch AR09_4digit (saved by Fritzing 0.9.3b)
breadboards: 1

parts:
  R1 = Resistor [tolerance=±5% resistance=330 package=THT]
  R2 = Resistor [tolerance=±5% resistance=330 package=THT]
  R3 = Resistor [tolerance=±5% resistance=330 package=THT]
  R4 = Resistor [tolerance=±5% resistance=330 package=THT]
  R5 = Resistor [tolerance=±5% resistance=330 package=THT]
  R6 = Resistor [tolerance=±5% resistance=330 package=THT]
  R7 = Resistor [tolerance=±5% resistance=330 package=THT]
  R8 = Resistor [tolerance=±5% resistance=330 package=THT]
  U1 = 7-SEGMENT-4DIGIT [package=7-segment-4digit-5641]
  부품2 = Arduino Uno (Rev3)

nets:
  N1: R1.Pin_0, 부품2.D6_PWM
  N2: R1.Pin_1, U1.A
  N3: R2.Pin_0, 부품2.D5_PWM
  N4: R2.Pin_1, U1.D
  N5: R3.Pin_0, U1.F
  N6: R3.Pin_1, 부품2.D7
  N7: R4.Pin_0, U1.G
  N8: R4.Pin_1, 부품2.D8
  N9: R5.Pin_0, U1.B
  N10: R5.Pin_1, 부품2.D3_PWM
  N11: R6.Pin_0, U1.C
  N12: R6.Pin_1, 부품2.D4
  N13: R7.Pin_1, U1.DP
  N14: R8.Pin_0, 부품2.D2
  N15: R8.Pin_1, U1.E
  N16: U1.DIG2, 부품2.D11_PWM/MOSI
  N17: U1.DIG3, 부품2.D12/MISO
  N18: U1.DIG4, 부품2.D13/SCK
  N19: U1.DIG1, 부품2.D10_PWM/SS

custom parts:
  7-SEGMENT-4DIGIT: if you need make parts, send me e-mail and write. Price 1 part=0.9 WMZ (http://www.wmtransfer.com/) ~ 0.9 Euro
